// Logisim project Exp-5.circ as structural Verilog: 1 circuit, main circuit main
module main (
  input  in_1,
  input  in_2,
  input  in_3,
  output out_4,
  output out_5,
  output out_6
);

  wire clock_1_out, clock_2_out, j_k_ff_1_qn, t_ff_1_qn;

  Clock clock_1 (.out(clock_1_out));
  Clock clock_2 (.out(clock_2_out));
  J_K_Flip_Flop j_k_ff_1 (.J(in_2), .clk(clock_2_out), .K(in_2), .Qn(j_k_ff_1_qn));  // open: Q, preset, en, reset
  T_Flip_Flop t_ff_1 (.clk(clock_1_out), .T(in_1), .Q(out_4), .Qn(t_ff_1_qn));  // open: preset, reset, en
  T_Flip_Flop t_ff_2 (.clk(t_ff_1_qn), .T(in_1), .Q(out_5));  // open: Qn, preset, reset, en
  J_K_Flip_Flop j_k_ff_2 (.J(in_3), .clk(j_k_ff_1_qn), .K(in_3), .Q(out_6));  // open: Qn, preset, en, reset

  // Notes on the sheet:
  //   2-Bit (MOD 4) Ripple Counter 
  //   -------------------------------------------------------------------------------------------------------------------------------------------------------------------------------------------------------------------------------------------------------------------------------------------------------------------------------------------------------------------------------------------------------------------------------------------------------------------------------
endmodule
