// Logisim project JK 0-0.circ as structural Verilog: 1 circuit, main circuit main
module main (
  input  J,
  input  K,
  output Q,
  output Q_prime
);

  wire clock_1_out, NAND_2_out, NAND_out;

  Clock clock_1 (.out(clock_1_out));
  nand NAND (NAND_out, Q_prime, J, clock_1_out);
  nand NAND_2 (NAND_2_out, clock_1_out, K, Q);
  nand NAND_3 (Q, NAND_out, Q_prime);
  nand NAND_4 (Q_prime, Q, NAND_2_out);

  // Notes on the sheet:
  //   CLK
  //   JK Flip Flop
  //   JK Flip Flop MASTER-SLAVE
endmodule
